# Fritzing sketch circuit-design (saved by Fritzing 0.9.3b)
circuit board: 8.46667cm x 5.64444cm

parts:
  WeMos_D1_Mini2 = WeMos D1 Mini
  DEC-Nema17 = Stepper Motor - Bipolar
  FOC-Nema11 = Stepper Motor - Bipolar
  CNC3 = Arduino_CNC_V3.00
  RA-Nema_17 = Stepper Motor - Bipolar
  ZS-042_RTC1 = ZS-042 RTC Module
  Componente1 = Adafruit BMP280 [part_number="Adafruit #2651"]
  ANT1 = Antenna  # not connected
  19V = Power plug
  VREG = LM2596 step down module
  FAN = Fan - Ventilador [package=THT]
  WeMos_D1_R32 = Arduino Uno (Rev3)

nets:
  5V: WeMos_D1_Mini2.5V, CNC3.5V
  N1: WeMos_D1_Mini2.G, CNC3.GND
  N2: WeMos_D1_Mini2.RX, CNC3.End_Stops_Y-_(and_Y+)
  N3: WeMos_D1_Mini2.TX, CNC3.End_Stops_X-_(and_X+)
  N4: DEC-Nema17.A, CNC3.Y-MTR_'4'
  N5: DEC-Nema17.C, CNC3.Y-MTR_'3'
  N6: DEC-Nema17.B, CNC3.Y-MTR_'2'
  N7: DEC-Nema17.D, CNC3.Y-MTR_'1'
  N8: FOC-Nema11.A, CNC3.Z-MTR_'1'
  N9: FOC-Nema11.C, CNC3.Z-MTR_'2'
  N10: FOC-Nema11.B, CNC3.Z-MTR_'3'
  N11: FOC-Nema11.D, CNC3.Z-MTR_'4'
  GND: CNC3.POWER_-, 19V.GND, VREG.IN-, VREG.OUT-, FAN.GND
  N12: CNC3.POWER_+, 19V.VCC, VREG.IN+
  N13: CNC3.X_-_M0, CNC3.SpnDir
  N14: CNC3.X_-_M1, CNC3.SpnEn_/_Z_Limit
  N15: CNC3.X-MTR_'1', RA-Nema_17.D
  N16: CNC3.X-MTR_'2', RA-Nema_17.B
  N17: CNC3.X-MTR_'3', RA-Nema_17.C
  N18: CNC3.X-MTR_'4', RA-Nema_17.A
  N19: CNC3.Y_-_M0, CNC3.Hold
  N20: CNC3.Y_-_M1, CNC3.Abort
  N21: CNC3.3V3, ZS-042_RTC1.VCC#1
  N22: CNC3.End_Stops_Z+_(Gnd), ZS-042_RTC1.GND#0
  N23: ZS-042_RTC1.SDA#2, WeMos_D1_R32.A4/SDA
  N24: ZS-042_RTC1.SCL#3, WeMos_D1_R32.A5/SCL
  N25: ZS-042_RTC1.GND#6, Componente1.GND
  N26: ZS-042_RTC1.VCC#7, Componente1.VCC, Componente1.SDO/ADR, Componente1.CS
  N27: ZS-042_RTC1.SDA#8, Componente1.SDI/SDA
  N28: ZS-042_RTC1.SCL#9, Componente1.SCK/SCL
  N29: VREG.OUT+, FAN.5V

custom parts:
  Arduino_CNC_V3.00: Protoneer Arduino CNC Shield V3.00 If using Grbl V0.9: The “A” axis can not be used (yet). The “SCL” (Arduino A5) pin is now used for 'Probing' input. The “End Stops Z+ & Z-” (Arduino D11) and “SpnEn” (Arduino D12) have been switched!
  Adafruit BMP280: Bosch has stepped up their game with their new BMP280 sensor, an environmental sensor with temperature, barometric pressure that is the next generation upgrade to the BMP085/BMP180/BMP183. This sensor is great for all sorts of weather sensing and can even be used in both I2C and SPI! This precision sensor from Bosch is the best low-cost, precision sensing solution for measuring barometric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
  LM2596 step down module: LM2596 DC-DC step down power supply module 3 A.
  Fan - Ventilador: Ventilador de 2 pines, se encuentra comunmente en computadoras de escritorio
